# Fritzing sketch Circuit_connection (saved by Fritzing 0.9.3b)
circuit board: 8.46667cm x 5.64444cm
breadboards: 2

parts:
  Part1 = Arduino Uno (Rev3)
  8_Channel_Relay1 = 8 Channel Power Relay
  Part2 = Arduino Uno (Rev3)
  LED1 = smd LED [color="Red (633nm)" package="1206 [SMD]"]
  R1 = Resistor [tolerance=±5% resistance=220 package=THT]
  VCC1 = Battery block 9V
  LED2 = smd LED [color="Red (633nm)" package="1206 [SMD]"]
  R2 = Resistor [tolerance=±5% resistance=220 package=THT]
  LED3 = smd LED [color="Red (633nm)" package="1206 [SMD]"]
  R3 = Resistor [tolerance=±5% resistance=220 package=THT]
  LED4 = smd LED [color="Red (633nm)" package="1206 [SMD]"]
  R4 = Resistor [tolerance=±5% resistance=220 package=THT]
  LED5 = smd LED [color="Red (633nm)" package="1206 [SMD]"]
  R5 = Resistor [tolerance=±5% resistance=220 package=THT]
  LED6 = smd LED [color="Red (633nm)" package="1206 [SMD]"]
  R6 = Resistor [tolerance=±5% resistance=220 package=THT]
  LED7 = smd LED [color="Red (633nm)" package="1206 [SMD]"]
  R7 = Resistor [tolerance=±5% resistance=220 package=THT]
  M1 = fc-51 [package=THT]
  M2 = fc-51 [package=THT]
  M3 = fc-51 [package=THT]
  M4 = fc-51 [package=THT]
  M5 = fc-51 [package=THT]
  M6 = fc-51 [package=THT]
  M7 = fc-51 [package=THT]

nets:
  N1: Part1.D8, 8_Channel_Relay1.IN4
  N2: Part1.D9_PWM, 8_Channel_Relay1.IN3
  N3: Part1.D10_PWM/SS, 8_Channel_Relay1.IN2
  N4: Part1.D11_PWM/MOSI, 8_Channel_Relay1.IN1
  GND: Part1.GND, 8_Channel_Relay1.GND
  N5: Part1.D0/RX, Part2.D1/TX
  N6: Part1.D1/TX, Part2.D0/RX
  N7: Part1.D5_PWM, 8_Channel_Relay1.IN7
  N8: Part1.D6_PWM, 8_Channel_Relay1.IN6
  N9: Part1.D7, 8_Channel_Relay1.IN5
  5V: Part1.5V, 8_Channel_Relay1.VCC
  N10: 8_Channel_Relay1.COM, VCC1.+
  N11: 8_Channel_Relay1.NO#23, LED1.cathode
  N12: 8_Channel_Relay1.NO#26, LED2.cathode
  N13: 8_Channel_Relay1.NO#29, LED3.cathode
  N14: 8_Channel_Relay1.NO#32, LED4.cathode
  N15: 8_Channel_Relay1.NO#35, LED5.cathode
  N16: 8_Channel_Relay1.NO#38, LED6.cathode
  N17: 8_Channel_Relay1.NO#41, LED7.cathode
  N18: Part2.D8, M4.pin1
  N19: Part2.D9_PWM, M3.pin1
  N20: Part2.D10_PWM/SS, M2.pin1
  N21: Part2.D11_PWM/MOSI, M1.pin1
  N22: Part2.D5_PWM, M7.pin1
  N23: Part2.D6_PWM, M6.pin1
  N24: Part2.D7, Part2.5V, M1.pin2, M1.pin3, M2.pin2, M2.pin3, M3.pin2, M3.pin3, M4.pin2, M4.pin3, M5.pin2, M5.pin3, M6.pin2, M6.pin3, M7.pin2, M7.pin3
  N25: LED1.anode, R1.Pin_0
  N26: R1.Pin_1, VCC1.-, R2.Pin_1, R3.Pin_1, R4.Pin_1, R5.Pin_1, R6.Pin_1, R7.Pin_1
  N27: LED2.anode, R2.Pin_0
  N28: LED3.anode, R3.Pin_0
  N29: LED4.anode, R4.Pin_0
  N30: LED5.anode, R5.Pin_0
  N31: LED6.anode, R6.Pin_0
  N32: LED7.anode, R7.Pin_0

custom parts:
  8 Channel Power Relay: An 8 channel power relay. The module operates at 5V.
